# Fritzing sketch heart_project (saved by Fritzing 1.0.4)
breadboards: 4

parts:
  U1 = LCD-16X2 [package=lcd-16x2]
  R1 = Rotary Potentiometer (Small) [maximum_resistance=10kΩ knob_status=50% power=0.5W package=THT]
  R2 = Resistor [tolerance=±5% power=0.25W resistance=220 package=THT]
  Next = Pushbutton [package="[THT]"]
  Back = Pushbutton [package="[THT]"]
  Select = Pushbutton [package="[THT]"]
  Previous = Pushbutton [package="[THT]"]
  Bauteil2 = Arduino Mega ADK (Rev3)
  LED1 = RGB LED (com. cathode, rbg) [color="Red (633nm)" current=0.030A package="5 mm [THT]"]
  LED2 = RGB LED (com. cathode, rbg) [color="Red (633nm)" current=0.030A package="5 mm [THT]"]
  LED3 = RGB LED (com. cathode, rbg) [color="Red (633nm)" current=0.030A package="5 mm [THT]"]
  LED4 = RGB LED (com. cathode, rbg) [color="Red (633nm)" current=0.030A package="5 mm [THT]"]
  LED5 = RGB LED (com. cathode, rbg) [color="Red (633nm)" current=0.030A package="5 mm [THT]"]
  LED6 = RGB LED (com. cathode, rbg) [color="Red (633nm)" current=0.030A package="5 mm [THT]"]
  LED7 = RGB LED (com. cathode, rbg) [color="Red (633nm)" current=0.030A package="5 mm [THT]"]
  LED8 = RGB LED (com. cathode, rbg) [color="Red (633nm)" current=0.030A package="5 mm [THT]"]
  LED9 = RGB LED (com. cathode, rbg) [color="Red (633nm)" current=0.030A package="5 mm [THT]"]
  LED10 = RGB LED (com. cathode, rbg) [color="Red (633nm)" current=0.030A package="5 mm [THT]"]
  Bauteil3 = Adafruit PCA9685 PWM/Servo Breakout [part_number=815]
  Bauteil4 = Adafruit PCA9685 PWM/Servo Breakout [part_number=815]
  VCC1 = 4 x AAA Battery Mount [internal_resistance=0.1Ω]
  R3 = Rotary Potentiometer (Small) [maximum_resistance=100kΩ knob_status=50% power=0.5W package=THT]
  R4 = Rotary Potentiometer (Small) [maximum_resistance=100kΩ knob_status=50% power=0.5W package=THT]
  R5 = Rotary Potentiometer (Small) [maximum_resistance=100kΩ knob_status=50% power=0.5W package=THT]
  R6 = Rotary Potentiometer (Small) [maximum_resistance=100kΩ knob_status=50% power=0.5W package=THT]
  HC-SR04_Sensor_1 = HC-SR04 Ultrasonic Distance Sensor
  U2 = TMP36 [package=to-92-kit]
  Q1 = LTR-301 [package=ltr-301]
  R7 = Resistor [tolerance=±5% power=0.25W resistance=10k package=THT]
  IR1 = TSOP312.., 314.. [package=THT]
  Bauteil5 = Bluetooth HC-05 Macho
  R8 = Resistor [tolerance=±5% power=0.25W resistance=2.2k package=THT]
  R10 = Resistor [tolerance=±5% power=0.25W resistance=10k package=THT]
  R12 = Resistor [tolerance=±5% power=0.25W resistance=2.2k package=THT]

nets:
  GND: U1.VSS, U1.R_W, U1.K, R1.leg2, Next.Pin_1, Next.Pin_2, Back.Pin_1, Back.Pin_2, Select.Pin_1, Select.Pin_2, Previous.Pin_1, Previous.Pin_2, Bauteil2.GND, LED1.common_cathode, LED2.common_cathode, LED3.common_cathode, LED4.common_cathode, LED5.common_cathode, LED6.common_cathode, LED7.common_cathode, LED8.common_cathode, LED9.common_cathode, LED10.common_cathode, Bauteil3.GND, Bauteil4.GND, VCC1.-, R3.leg2, R4.leg2, R5.leg2, R6.leg2, HC-SR04_Sensor_1.GND, U2.GND, R7.Pin_1, IR1.GND
  VCC: U1.VDD, R1.leg1, R2.Pin_1, Bauteil2.5V, Bauteil3.VCC, Bauteil4.VCC, R3.leg1, R4.leg1, R5.leg1, R6.leg1, HC-SR04_Sensor_1.VCC, U2.VCC, Q1.C, IR1.Vs, Bauteil5.VCC
  N1: U1.VO, R1.wiper
  N2: U1.RS, Bauteil2.D12_PWM
  N3: U1.E, Bauteil2.D11_PWM
  N4: U1.DB4, Bauteil2.D5_PWM
  N5: U1.DB5, Bauteil2.D4_PWM
  N6: U1.DB6, Bauteil2.D3_PWM
  N7: U1.DB7, Bauteil2.D2_PWM
  N8: U1.A, R2.Pin_0
  N9: Next.Pin_3, Next.Pin_4, Bauteil2.D8_PWM
  N10: Back.Pin_3, Back.Pin_4, Bauteil2.D6_PWM
  N11: Select.Pin_3, Select.Pin_4, Bauteil2.D7_PWM
  N12: Previous.Pin_3, Previous.Pin_4, Bauteil2.D9_PWM
  N13: Bauteil2.A0, R6.wiper
  N14: Bauteil2.A1, R5.wiper
  N15: Bauteil2.A2, R4.wiper
  N16: Bauteil2.A3, R3.wiper
  N17: Bauteil2.A4, U2.VOUT
  N18: Bauteil2.D21/SCL, Bauteil3.SCL, Bauteil4.SCL
  N19: Bauteil2.D20/SDA, Bauteil3.SDA, Bauteil4.SDA
  N20: Bauteil2.D19/RX1, Bauteil5.TXD
  N21: Bauteil2.D18/TX1, R12.Pin_1
  N22: Bauteil2.D13_PWM, HC-SR04_Sensor_1.TRIG
  N23: Bauteil2.D10_PWM, HC-SR04_Sensor_1.ECHO
  N24: Bauteil2.D22, IR1.Data
  N25: Bauteil2.D23, Q1.E, R7.Pin_0
  N26: Bauteil2.D24, Bauteil5.State
  N27: Bauteil2.D25, Bauteil5.Key, R10.Pin_0
  N28: LED1.red_anode, Bauteil3.PWM12
  N29: LED1.blue_anode, Bauteil3.PWM13
  N30: LED1.green_anode, Bauteil3.PWM14
  N31: LED2.red_anode, Bauteil3.PWM9
  N32: LED2.blue_anode, Bauteil3.PWM10
  N33: LED2.green_anode, Bauteil3.PWM11
  N34: LED3.red_anode, Bauteil3.PWM6
  N35: LED3.blue_anode, Bauteil3.PWM7
  N36: LED3.green_anode, Bauteil3.PWM8
  N37: LED4.red_anode, Bauteil3.PWM3
  N38: LED4.blue_anode, Bauteil3.PWM4
  N39: LED4.green_anode, Bauteil3.PWM5
  N40: LED5.red_anode, Bauteil3.PWM0
  N41: LED5.blue_anode, Bauteil3.PWM1
  N42: LED5.green_anode, Bauteil3.PWM2
  N43: LED6.red_anode, Bauteil4.PWM12
  N44: LED6.blue_anode, Bauteil4.PWM13
  N45: LED6.green_anode, Bauteil4.PWM14
  N46: LED7.red_anode, Bauteil4.PWM9
  N47: LED7.blue_anode, Bauteil4.PWM10
  N48: LED7.green_anode, Bauteil4.PWM11
  N49: LED8.red_anode, Bauteil4.PWM6
  N50: LED8.blue_anode, Bauteil4.PWM7
  N51: LED8.green_anode, Bauteil4.PWM8
  N52: LED9.red_anode, Bauteil4.PWM3
  N53: LED9.blue_anode, Bauteil4.PWM4
  N54: LED9.green_anode, Bauteil4.PWM5
  N55: LED10.red_anode, Bauteil4.PWM0
  N56: LED10.blue_anode, Bauteil4.PWM1
  N57: LED10.green_anode, Bauteil4.PWM2
  N58: Bauteil3.5.0V, Bauteil4.5.0V, VCC1.+
  N59: Bauteil5.RXD, R8.Pin_1
  N60: Bauteil5.GND, R8.Pin_0

custom parts:
  Adafruit PCA9685 PWM/Servo Breakout: Using only two pins, control 16 free-running PWM outputs! I2C-controlled PWM driver with a built in clock. Unlike the TLC5940 family, you do not need to continuously send it signal tying up your microcontroller, its completely free running! 5V compliant, which means you can control it from a 3.3V microcontroller and still safely drive up to 6V outputs (this is good for when you want to control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
